# Fritzing sketch schematic (saved by Fritzing 0.9.3b)
breadboards: 1

parts:
  U1 = NodeMCU V1.0
  Power_plug1 = Power plug
  U2 = Mini-360 DC-DC Buck converter [package=THT]
  U3 = Hirose DF13 Series Header [part_number=DF13#-3P-1.25V package=DF13C-3P-1.25V]
  TRRS1 = Audio Jack (TRRS) 3.5mm [part_number="LUMBERG JEITA RC-5325A" package="RC-5325A [SMD]"]  # not connected
  74AHCT125 = SO14 [chip_label=74AHCT125 package=SO]

nets:
  N1: U1.D1, 74AHCT125.2
  GND: U1.GND, Power_plug1.GND, U2.IN-, U2.OUT-, U3.3, 74AHCT125.1, 74AHCT125.7
  N2: U1.Vin, U2.OUT+, 74AHCT125.14
  N3: Power_plug1.VCC, U2.IN+, U3.1
  N4: U3.2, 74AHCT125.3

notes:
  12V
  Data
  GND
  RGB LED Strip Connector

custom parts:
  NodeMCU V1.0: ESP8266 based NodeMCU
  Mini-360 DC-DC Buck converter: Mini-360 DC-DC Buck converter. Tiny buck step down voltage converter, input voltage 4.75 to 23V output 1 to 17V adjustable. Available from ebay and the like.
